# Fritzing sketch 智慧插座 (saved by Fritzing 0.9.10b)
breadboards: 1

parts:
  ESP32 = lilygo t-display-S3
  U1 = MAX6675 [package=so08]
  電壓感測模組 = zmpt101b
  電流感測模組 = ACS712 [package=so08]
  電流感測模組_2 = ACS712 [package=so08]

nets:
  N1: ESP32.Pin_5, U1.CS
  N2: ESP32.Pin_6, U1.SCK
  N3: ESP32.Pin_7, U1.MISO
  N4: ESP32.Pin_10, ESP32.Pin_11, U1.VSS
  VCC: ESP32.Pin_15, ESP32.Pin_28, 電壓感測模組.VCC, 電流感測模組.VCC, 電流感測模組_2.VCC
  N5: ESP32.Pin_17, U1.VDD
  N6: ESP32.Pin_25, 電壓感測模組.OUT
  N7: ESP32.Pin_26, 電流感測模組_2.VOUT
  N8: ESP32.Pin_27, 電流感測模組.VOUT
  GND: 電壓感測模組.GND, 電流感測模組.GND, 電流感測模組_2.GND

custom parts:
  lilygo t-display-S3: T-Display-S3 ESP32-S3 1.9 inch ST7789 LCD Display Development Board WIFI Bluetooth5.0 Wireless Module 170*320 Resolution.
  zmpt101b: Single phase ac active output voltate transformer module.
